# Fritzing sketch tesis (saved by Fritzing 0.9.3b)

parts:
  MOTOR_12VDC = DC Motor
  Motor_brushless_12VDC = Brushless Motor
  Motor_brushless_12VDC_2 = Brushless Motor
  LM35 = LM35 Temperature Sensor [package="TO92 [THT]"]
  LM35_2 = LM35 Temperature Sensor [package="TO92 [THT]"]
  HC-SR4 = hc-sr04
  4CH_Relay = 4-Channel 5v Relay Shield [package=relay-4ch5v10a]
  2CH_Relay = 2-Channel 5v Relay Shield [package=relay-2ch5v10a]
  Ultrasonic_humidifier = Vibration Motor- ROB-08449 [package=vibe-motor-10mm]
  Componente1 = Arduino Uno (Rev3) - ICSP
  Driver_MOSFET_IRF520 = IFR520 MOS module [package=THT]
  Motor_12VDC = DC Motor
  MQ-7 = MQ-7 breakout
  Transformador = Transformer [package=transformer]
  LED_Grow = RGB Strip LED
  5V = female pin header, 1 pin [form="♀ (female)"]
  GND = female pin header, 1 pin [form="♀ (female)"]
  GND_2 = female pin header, 1 pin [form="♀ (female)"]
  5V_2 = female pin header, 1 pin [form="♀ (female)"]
  GND_3 = female pin header, 1 pin [form="♀ (female)"]
  5v = female pin header, 1 pin [form="♀ (female)"]
  GND_4 = female pin header, 1 pin [form="♀ (female)"]
  12V = female pin header, 1 pin [form="♀ (female)"]
  GND_5 = female pin header, 1 pin [form="♀ (female)"]
  12V_2 = female pin header, 1 pin [form="♀ (female)"]
  GND_6 = female pin header, 1 pin [form="♀ (female)"]
  220VAC = Power plug
  12V_3 = female pin header, 1 pin [form="♀ (female)"]
  12V_4 = female pin header, 1 pin [form="♀ (female)"]
  12V_5 = female pin header, 1 pin [form="♀ (female)"]
  GND_7 = female pin header, 1 pin [form="♀ (female)"]
  12V_6 = female pin header, 1 pin [form="♀ (female)"]
  GND_8 = female pin header, 1 pin [form="♀ (female)"]
  5V_3 = female pin header, 1 pin [form="♀ (female)"]
  GND_9 = female pin header, 1 pin [form="♀ (female)"]
  S1 = H-Bridge with L298N
  GND_10 = female pin header, 1 pin [form="♀ (female)"]
  Motor_12VDC1 = DC Motor

nets:
  N1: MOTOR_12VDC.pin_1, S1.M2-02
  N2: MOTOR_12VDC.pin_2, S1.M2-01
  N3: Motor_brushless_12VDC.A, 4CH_Relay.K3-Off
  N4: Motor_brushless_12VDC.C, GND_6.pin1
  N5: Motor_brushless_12VDC_2.A, 12V_2.pin1
  N6: Motor_brushless_12VDC_2.B, Componente1.D5_PWM
  N7: Motor_brushless_12VDC_2.C, 2CH_Relay.K1-In
  N8: LM35.+Vs, 5v.pin1
  N9: LM35.Vout, Componente1.A5/SCL
  N10: LM35.GND, GND_3.pin1
  N11: LM35_2.+Vs, 5V.pin1
  N12: LM35_2.Vout, Componente1.A0
  N13: LM35_2.GND, GND.pin1
  N14: HC-SR4.VCC, 5V_3.pin1
  N15: HC-SR4.Trig, HC-SR4.Echo, Componente1.D6_PWM
  N16: HC-SR4.GND, GND_9.pin1
  N17: 4CH_Relay.IN1, Componente1.D13/SCK
  N18: 4CH_Relay.IN2, Componente1.ICSP_MISO, Componente1.D12/MISO
  N19: 4CH_Relay.K1-Off, Motor_12VDC.pin_1, Motor_12VDC.pin_2, GND_7.pin1
  N20: 4CH_Relay.K1-On, 12V_5.pin1
  N21: 4CH_Relay.K2-Off, Motor_12VDC1.pin_1
  N22: 4CH_Relay.K2-On, 12V_4.pin1
  N23: 4CH_Relay.IN4, Componente1.D7
  N24: 4CH_Relay.K3-On, 12V_3.pin1
  N25: 4CH_Relay.K4-Off, Transformador.2
  N26: 4CH_Relay.K4-On, Transformador.4, 220VAC.VCC
  N27: 4CH_Relay.IN3, Componente1.D10_PWM/SS
  N28: 2CH_Relay.VCC, 2CH_Relay.IN2, Componente1.D2
  N29: 2CH_Relay.GND, 2CH_Relay.IN1, Componente1.D4
  N30: 2CH_Relay.K1-On, GND_5.pin1
  N31: 2CH_Relay.K2-In, Ultrasonic_humidifier.-
  N32: 2CH_Relay.K2-On, 12V_6.pin1
  N33: Ultrasonic_humidifier.+, GND_8.pin1
  N34: Componente1.A1, MQ-7.DO
  N35: Componente1.D8, S1.IN1
  N36: Componente1.D9_PWM, S1.IN2
  N37: Componente1.D3_PWM, Driver_MOSFET_IRF520.pin1, Driver_MOSFET_IRF520.pin2
  N38: Driver_MOSFET_IRF520.pin4, LED_Grow.Common_Connect#4
  N39: Driver_MOSFET_IRF520.pin5, LED_Grow.Blue_Connect#5
  N40: Driver_MOSFET_IRF520.pin6, 12V.pin1
  N41: Driver_MOSFET_IRF520.pin7, GND_4.pin1
  N42: MQ-7.VCC, 5V_2.pin1
  N43: MQ-7.GND, GND_2.pin1
  N44: Transformador.1, 220VAC.GND
  N45: GND_10.pin1, Motor_12VDC1.pin_2

custom parts:
  Brushless Motor: A standard Brushless DC motor
  4-Channel 5v Relay Shield: 4 Channel 5v Relay Shield w. 2x SPD-06VDC-SD-C
  2-Channel 5v Relay Shield: 2 Channel 5v Relay Shield w. 2x SPD-06VDC-SD-C
  MQ-7 breakout: SKU: 101282
  RGB Strip LED: A tri-color Strip LED with red, green and blue. Pin order: red - common cathode - blue - green
  H-Bridge with L298N: h-bridge
